// Logisim project 8-bit Computer Simulation.circ as structural Verilog: 5 circuits, main circuit Register A
module Register_A (
  input  in_1,
  input  Enable,
  input  Clear,
  input  in_4,
  input  in_5,
  input  in_6,
  input  in_7,
  input  in_8,
  input  in_9,
  input  in_10,
  input  CLR,
  output out_12,
  output out_13,
  output out_14,
  output out_15,
  output out_16,
  output out_17,
  output out_18,
  output out_19
);

  wire [7:0] RA_q;

  Clock Clock (.out(Enable));
  Register RA (.D({in_10, in_9, in_8, in_7, in_6, in_5, in_4, in_1}), .en(Enable), .Q(RA_q), .clk(Enable), .clr(Clear));
  assign {out_19, out_18, out_17, out_16, out_15, out_14, out_13, out_12} = CLR ? RA_q : 8'bz;  // Controlled_Buffer controlled_buffer_1

  // Notes on the sheet:
  //   Register A
endmodule

module Registr_B (
  input  in_1,
  input  in_2,
  input  in_3
);

  wire [7:0] controlled_buffer_1_out, RB_q, undriven;

  Register RB (.D(undriven), .en(in_1), .Q(RB_q), .clk(in_1));  // open: clr
  Clock clock_1 (.out(in_1));
  assign controlled_buffer_1_out = in_3 ? RB_q : 8'bz;  // Controlled_Buffer controlled_buffer_1
endmodule

// ALU
module ALU_1_bit (
  input  [2:0] in_1,
  input  Sub,
  input  Cin,
  input  A,
  input  B,
  input  less,
  output Result,
  output Cout,
  output set
);

  wire and_1_out, nor_1_out, or_1_out, xor_1_out, xor_2_out;

  xor xor_1 (xor_1_out, B, Sub);
  Adder #(.width(1)) adder_1 (.a(A), .b(xor_1_out), .out(set), .cin(Cin), .cout(Cout));
  and and_1 (and_1_out, A, B);
  or or_1 (or_1_out, A, B);
  xor xor_2 (xor_2_out, A, B);
  nor nor_1 (nor_1_out, A, B);
  Multiplexer #(.select(3), .enable("false")) multiplexer_1 (
    .in0(and_1_out), .in1(or_1_out), .in2(xor_2_out), .in3(nor_1_out), .in4(set), .in5(less), .in6(Cout),
    .in7(set), .out(Result), .sel(in_1));
endmodule

module ALu (
  input  Sub,
  input  [2:0] OP,
  input  [7:0] A,
  input  [7:0] B,
  output [7:0] R,
  output Zero
);

  wire alu_1_bit_1_cout, alu_1_bit_2_p5, alu_1_bit_3_p5, alu_1_bit_4_p5, alu_1_bit_5_p5, alu_1_bit_6_p5,
       alu_1_bit_7_p5, alu_1_bit_8_p6;

  ALU_1_bit alu_1_bit_1 (
    .in_1(OP), .A(A[0]), .B(B[0]), .less(alu_1_bit_8_p6), .Result(R[0]), .Sub(Sub), .Cout(alu_1_bit_1_cout));  // open: set, Cin
  // ALU_1_bit alu_1_bit_2: pin names not known; wires that end beside it: A[1], B[1], 1'b0, Sub, alu_1_bit_2_p5, alu_1_bit_1_cout, OP, R[1]
  // ALU_1_bit alu_1_bit_3: pin names not known; wires that end beside it: A[2], B[2], 1'b0, Sub, alu_1_bit_3_p5, alu_1_bit_2_p5, OP, R[2]
  // ALU_1_bit alu_1_bit_4: pin names not known; wires that end beside it: A[3], B[3], 1'b0, Sub, alu_1_bit_4_p5, alu_1_bit_3_p5, OP, R[3]
  // ALU_1_bit alu_1_bit_5: pin names not known; wires that end beside it: A[4], B[4], 1'b0, Sub, alu_1_bit_5_p5, alu_1_bit_4_p5, OP, R[4]
  // ALU_1_bit alu_1_bit_6: pin names not known; wires that end beside it: A[5], B[5], 1'b0, Sub, alu_1_bit_6_p5, alu_1_bit_5_p5, OP, R[5]
  // ALU_1_bit alu_1_bit_7: pin names not known; wires that end beside it: A[6], B[6], 1'b0, Sub, alu_1_bit_7_p5, alu_1_bit_6_p5, OP, R[6]
  // ALU_1_bit alu_1_bit_8: pin names not known; wires that end beside it: A[7], B[7], 1'b0, Sub, alu_1_bit_7_p5, alu_1_bit_8_p6, OP, R[7]
  nor nor_1 (Zero, R[0], R[1], R[2], R[3], R[4], R[5], R[6], R[7]);
endmodule

module RAM (
);

  RAM_part #(.addrWidth(4)) ram_1 ();  // open: addr, data, sel, clk, ld, clr
endmodule
